# Fritzing sketch voiture_commande_gestuelle (saved by Fritzing 0.9.3b)
breadboards: 1

parts:
  S1 = H-Bridge with L298N
  Composant1 = Arduino Uno (Rev3)
  Composant2 = InvenSense MPU6050
  U1 = RF-LINK_TX [package=rf-link_tx]
  U2 = RF-LINK_RX [package=rf-link_rx]
  Composant3 = LilyPad Coin Cell Battery Holder
  Composant5 = Lilypad Arduino Board
  VCC1 = 4 x AAA Battery Mount
  HC-SR04_Sensor_1 = HC-SR04 Ultrasonic Distance Sensor
  M4 = DC Motor
  S2 = H-Bridge with L298N
  J1 = Basic Servo
  M5 = DC Motor  # not connected
  M6 = DC Motor  # not connected
  M7 = DC Motor

nets:
  12V: S1.12V, VCC1.+, S2.12V
  GND: S1.GND, Composant1.GND, U2.GND, VCC1.-, HC-SR04_Sensor_1.GND, S2.GND
  N1: S1.IN1, Composant1.A2
  N2: S1.IN2, Composant1.A3
  N3: S1.IN3, Composant1.A4/SDA
  N4: S1.IN4, Composant1.A5/SCL
  N5: S1.OUT4-Motor2, M4.pin_1
  N6: Composant1.D8, HC-SR04_Sensor_1.ECHO
  N7: Composant1.D9_PWM, S2.IN4
  N8: Composant1.D10_PWM/SS, S2.IN2
  N9: Composant1.D12/MISO, J1.pulse
  N10: Composant1.D0/RX, U2.Data#2
  N11: Composant1.D2, S2.IN1
  N12: Composant1.D4, S2.IN3
  N13: Composant1.D7, HC-SR04_Sensor_1.TRIG
  VCC: Composant1.5V, U2.Data#3, U2.VCC, HC-SR04_Sensor_1.VCC
  VCC_2: Composant2.VCC, U1.+5V, Composant3.+, Composant5.VCC
  GND_2: Composant2.GND, U1.GND, Composant3.-, Composant5.GND
  N14: Composant2.SCL, Composant5.A1
  N15: Composant2.SDA, Composant5.A2
  N16: Composant2.INT, Composant5.D3
  N17: U1.DATA, Composant5.D2
  N18: S2.OUT4-Motor2, M7.pin_1

custom parts:
  H-Bridge with L298N: h-bridge
  RF-LINK_TX: Common RF transmitter of the 315.00Mhz varity
  RF-LINK_RX: RF Link receivers- WRL-8947, 8948, 8949, 8950
